// Logisim project 4bitALu.circ as structural Verilog: 3 circuits, main circuit LU
module LU (
  input  [3:0] A0,
  input  [3:0] B0,
  input  [2:0] SELECT,
  output [3:0] OUTPUT
);

  wire [3:0] and_1_out, and_2_out, and_3_out, nand_1_out, nor_1_out, not_1_out, not_2_out, or_1_out,
       xnor_1_out, xor_1_out;

  assign not_1_out = ~A0;  // NOT_Gate not_1, 4 bits wide
  assign not_2_out = ~B0;  // NOT_Gate not_2, 4 bits wide
  assign nand_1_out = ~(A0 & B0);  // NAND_Gate nand_1, 4 bits wide
  assign and_1_out = A0 & B0;  // AND_Gate and_1, 4 bits wide
  assign or_1_out = A0 | B0;  // OR_Gate or_1, 4 bits wide
  assign nor_1_out = ~(A0 | B0);  // NOR_Gate nor_1, 4 bits wide
  assign xor_1_out = A0 ^ B0;  // XOR_Gate xor_1, 4 bits wide
  assign xnor_1_out = ~(A0 ^ B0);  // XNOR_Gate xnor_1, 4 bits wide
  assign and_2_out = A0 & not_2_out;  // AND_Gate and_2, 4 bits wide
  assign and_3_out = not_1_out & not_2_out;  // AND_Gate and_3, 4 bits wide
  Multiplexer #(.select(3), .width(4), .enable("false")) multiplexer_1 (
    .in0(and_1_out), .in1(or_1_out), .in2(nand_1_out), .in3(nor_1_out), .in4(xor_1_out), .in5(xnor_1_out),
    .in6(and_2_out), .in7(and_3_out), .out(OUTPUT), .sel(SELECT));

  // Notes on the sheet:
  //   Logic Unit
  //   a xor b
  //   a xnor b
  //   a . b not
  //   anot . bnot
  //   a.b
  //   a or b
  //   a nand b
  //   a nor b
endmodule

module AU (
  input  [3:0] A,
  input  [3:0] B,
  input  [2:0] SELECT,
  output [3:0] OUTPUT,
  output carry_out
);

  wire adder_1_cout, adder_2_cout, or_1_out, or_2_out, or_3_out, subtractor_1_bout;
  wire [3:0] adder_1_out, adder_2_out, divider_1_out, multiplier_1_cout, multiplier_1_out, multiplier_2_cout,
       multiplier_2_out, multiplier_3_cout, multiplier_3_out, multiplier_4_cout, multiplier_4_out,
       negator_1_out, subtractor_1_out;

  Multiplier #(.width(4)) multiplier_1 (.a(A), .b(A), .out(multiplier_1_out), .cout(multiplier_1_cout));  // open: cin
  Adder #(.width(4)) adder_1 (.a(A), .b(B), .out(adder_1_out), .cout(adder_1_cout));  // open: cin
  Subtractor #(.width(4)) subtractor_1 (.a(A), .b(B), .out(subtractor_1_out), .bout(subtractor_1_bout));  // open: bin
  Multiplier #(.width(4)) multiplier_2 (.a(A), .b(B), .out(multiplier_2_out), .cout(multiplier_2_cout));  // open: cin
  Multiplier #(.width(4)) multiplier_3 (.a(A), .b(A), .out(multiplier_3_out), .cout(multiplier_3_cout));  // open: cin
  Divider #(.width(4)) divider_1 (.a(A), .b(B), .out(divider_1_out));  // open: upper, rem
  Negator #(.width(4)) negator_1 (.in(A), .out(negator_1_out));
  Adder #(.width(4)) adder_2 (.a(B), .b(B), .out(adder_2_out), .cout(adder_2_cout));  // open: cin
  Multiplier #(.width(4)) multiplier_4 (
    .a(multiplier_1_out), .b(A), .out(multiplier_4_out), .cin(multiplier_1_cout), .cout(multiplier_4_cout));
  Multiplexer #(.select(3), .width(4), .enable("false")) multiplexer_1 (
    .in0(adder_1_out), .in1(subtractor_1_out), .in2(multiplier_2_out), .in3(multiplier_3_out),
    .in4(divider_1_out), .in5(negator_1_out), .in6(adder_2_out), .in7(multiplier_4_out), .out(OUTPUT),
    .sel(SELECT));
  or or_1 (or_1_out, multiplier_2_cout[0], multiplier_2_cout[1], multiplier_2_cout[2], multiplier_2_cout[3]);
  or or_2 (or_2_out, multiplier_3_cout[0], multiplier_3_cout[1], multiplier_3_cout[2], multiplier_3_cout[3]);
  or or_3 (or_3_out, multiplier_4_cout[0], multiplier_4_cout[1], multiplier_4_cout[2], multiplier_4_cout[3]);
  Multiplexer #(.select(3), .enable("false")) multiplexer_2 (
    .in0(adder_1_cout), .in1(subtractor_1_bout), .in2(or_1_out), .in3(or_2_out), .in6(adder_2_cout),
    .in7(or_3_out), .out(carry_out), .sel(SELECT));  // open: in4, in5

  // Notes on the sheet:
  //   A+B
  //   CUBE(A)
  //   A-B
  //   A*B
  //   SQUARE(A)
  //   A/B
  //   NEGATION(A)
  //   B+B
  //   Arithmetic Unit
endmodule

module CU (
  input  [3:0] A,
  input  [3:0] B,
  input  [2:0] s1,
  input  [2:0] s2,
  input  SELECT_MUX,
  output out_6,
  output [3:0] op,
  output out_8,
  output out_9,
  output carry_flag
);

  wire and_1_out, and_2_out, not_2_out, not_3_out, not_4_out, or_1_out;
  wire [3:0] au_1_output, lu_1_output;

  LU lu_1 (.A0(A), .B0(B), .SELECT(s2), .OUTPUT(lu_1_output));
  AU au_1 (.A(A), .B(B), .SELECT(s1), .OUTPUT(au_1_output), .carry_out(carry_flag));
  Multiplexer #(.width(4), .enable("false")) multiplexer_1 (
    .in0(lu_1_output), .in1(au_1_output), .out(op), .sel(SELECT_MUX));
  or or_1 (or_1_out, op[0], op[1], op[2], op[3]);
  not not_1 (out_6, or_1_out);
  not not_2 (not_2_out, op[3]);
  and and_1 (and_1_out, not_2_out, B[3], A[3]);
  and and_2 (and_2_out, op[3], not_3_out, not_4_out);
  not not_3 (not_3_out, B[3]);
  not not_4 (not_4_out, A[3]);
  or or_2 (out_9, and_1_out, and_2_out);

  assign out_8 = op[3];

  // Notes on the sheet:
  //   Control Unit
  //   Zero flag
  //   overflow flag
  //   signed flag
endmodule
